# Fritzing sketch Sketch (saved by Fritzing 0.9.3b)
breadboards: 1

parts:
  Termistor = Temperature Sensor (Thermistor) [thermistor_type=PTC package=THT]
  R3 = Resistor [tolerance=±5% resistance=10k package=THT]
  Photocell = PHOTOCELL [package=photocell]
  R4 = Resistor [tolerance=±5% resistance=220 package=THT]
  LED1 = LED - 5mm [color="Red (633nm)" package="5 mm [THT]"]
  R5 = Resistor [tolerance=±5% resistance=10k package=THT]
  part = Arduino Uno (Rev3)

nets:
  N1: Termistor.pin_0, R3.Pin_1
  N2: Termistor.pin_1, Photocell.P$2, LED1.anode, part.5V
  N3: R3.Pin_0, R5.Pin_0, part.GND
  N4: Photocell.P$1, R5.Pin_1
  N5: R4.Pin_0, part.D13/SCK
  N6: R4.Pin_1, LED1.cathode
